# Fritzing sketch ldr-control (saved by Fritzing 0.9.2b)
breadboards: 1

parts:
  Part1 = Arduino Uno (Rev3)
  R1 = Photocell (LDR) [package=THT]
  R2 = Resistor [tolerance=±5% resistance=220 package=THT]
  R3 = Photocell (LDR) [package=THT]
  R4 = Resistor [tolerance=±5% resistance=220 package=THT]
  R5 = Photocell (LDR) [package=THT]
  R6 = Photocell (LDR) [package=THT]
  R7 = Resistor [tolerance=±5% resistance=220 package=THT]
  R8 = Resistor [tolerance=±5% resistance=220 package=THT]

nets:
  N1: Part1.A0, R1.pin_1, R2.Pin_0
  N2: Part1.A1, R3.pin_0, R4.Pin_1
  N3: Part1.A2, R6.pin_0, R7.Pin_1
  N4: Part1.A3, R5.pin_0, R8.Pin_1
  N5: Part1.GND, R1.pin_0, R3.pin_1, R6.pin_1
  N6: Part1.5V, R2.Pin_1, R4.Pin_0, R7.Pin_0, R8.Pin_0

notes:
  4 LDR connections for controlling the position in the 4 directions. (Up, Down, Left, Right)
  BLUE = Analog Pin Connecctions
